# Fritzing sketch O1Light - M5 ATOM Echo (saved by Fritzing 1.0.2b)

parts:
  Part1 = PowerBoost 500 Charger
  Part2 = Lithium Ion Polymer Battery 3.7v 500mAh [part_number=1578]
  S2 = Toggle Switch [package=THT]
  S3 = Pushbutton [package="[THT]"]
  U2 = Mystery Part - 9 pins [chip_label="M5 ATOM Echo" package=THT]

nets:
  N1: Part1.GND_BAT_IN, Part2.negative
  N2: Part1.VBAT_IN, Part2.positive
  N3: Part1.ENABLE, S2.COM
  N4: Part1.GND, S2.L2, S3.Pin_1, S3.Pin_2, U2.G
  N5: Part1.5.0V, U2.5V
  N6: S3.Pin_3, S3.Pin_4, U2.G21

custom parts:
  Lithium Ion Polymer Battery 3.7v 500mAh: Lithium ion polymer (also known as 'lipo' or 'lipoly') batteries are thin, light and powerful. The output ranges from 4.2V when completely charged to 3.7V. This battery has a capacity of 500mAh for a total of about 1.9 Wh. The batteries come pre-attached with a genuine 2-pin JST-PH connector as shown and include the necessary protection circuitry.
  Mystery Part - 9 pins: A dummy, proxy, ersatz, stand-in part for whatever you want. With 9 pins on a 100 mil inline pin header footprint.
